// Logisim project de pro b1.circ as structural Verilog: 1 circuit, main circuit main
module main (
  input  A,
  input  B,
  input  C,
  input  D,
  output F
);

  wire and_1_out, and_2_out, and_3_out, not_1_out, not_2_out, not_3_out, not_4_out;

  not not_1 (not_1_out, A);
  not not_2 (not_2_out, B);
  not not_3 (not_3_out, C);
  not not_4 (not_4_out, D);
  and and_1 (and_1_out, C, not_4_out);
  and and_2 (and_2_out, not_2_out, not_3_out);
  and and_3 (and_3_out, not_1_out, B, D);
  or or_1 (F, and_1_out, and_2_out, and_3_out);

  // Notes on the sheet:
  //   B'C'
  //      A'BD
  //   CD'
  //   CD'+B'C'+A'BD
endmodule
