// Logisim project de pro b3.circ as structural Verilog: 1 circuit, main circuit main
module main (
  input  B,
  input  Ty,
  input  Tr,
  input  C,
  input  RESET
);

  wire and_1_out, and_2_out, and_3_out, and_4_out, and_6_out, and_7_out, and_8_out, and_9_out, and_10_out,
       and_11_out, and_12_out, and_13_out, clock_1_out, E3, or_1_out, or_2_out, or_3_out, P, Q0, Q1;

  and and_1 (and_1_out, ~Q1, Q0);  // AND_Gate
  and and_2 (and_2_out, Q1, ~Q0);  // AND_Gate
  and and_3 (and_3_out, Q1, ~Q0, P);  // AND_Gate
  Clock clock_1 (.out(clock_1_out));
  or or_1 (or_1_out, and_1_out, and_2_out, and_3_out, and_4_out);
  and and_4 (and_4_out, Q1, Q0);  // AND_Gate
  D_Flip_Flop d_ff_1 (.clk(clock_1_out), .D(or_1_out), .Q(Q1), .reset(RESET));  // open: Qn, preset, en
  and and_5 (E3, Q1, ~Q0, P);  // AND_Gate
  and and_6 (and_6_out, P, ~E3);  // AND_Gate
  D_Flip_Flop d_ff_2 (.clk(clock_1_out), .D(or_2_out), .Q(P), .reset(RESET));  // open: Qn, preset, en
  and and_7 (and_7_out, ~Q1, Q0, ~Ty);  // AND_Gate
  and and_8 (and_8_out, Q1, ~Q0, Tr, P);  // AND_Gate
  and and_9 (and_9_out, Q1, Q0, ~C);  // AND_Gate
  or or_2 (or_2_out, B, and_6_out);
  and and_10 (and_10_out, ~Q1, ~Q0, P);  // AND_Gate
  D_Flip_Flop d_ff_3 (.clk(clock_1_out), .D(or_3_out), .Q(Q0), .reset(RESET));  // open: Qn, preset, en
  or or_3 (or_3_out, and_10_out, and_7_out, and_8_out, and_9_out);
  and and_11 (and_11_out, ~Q1, ~Q0);  // AND_Gate
  and and_12 (and_12_out, ~Q1, Q0);  // AND_Gate
  and and_13 (and_13_out, Q1, Q0);
  LED led_1 (.in(and_11_out));
  LED led_2 (.in(and_12_out));
  LED led_3 (.in(Q1));
  LED led_4 (.in(and_13_out));

  // Notes on the sheet:
  //   Q1
  //   P
  //   Q0
  //   GREEN
  //   YELLOW
  //   RED
  //   WALK
endmodule
