// Logisim project de pro b4.circ as structural Verilog: 1 circuit, main circuit main
module main (
  input  A,
  input  B,
  input  in_3,
  output Sum,
  output C_out
);

  wire and_1_out, and_2_out, and_3_out;

  ExactlyOne xor_1 (.out(Sum), .in0(A), .in1(B), .in2(in_3));
  and and_1 (and_1_out, A, B);
  and and_2 (and_2_out, A, in_3);
  and and_3 (and_3_out, B, in_3);
  or or_1 (C_out, and_1_out, and_2_out, and_3_out);
endmodule
