// Logisim project de pro b5.circ as structural Verilog: 1 circuit, main circuit main
module main (
);

  wire and_1_out, and_2_out, and_3_out, and_4_out, and_5_out, and_6_out, and_7_out, and_8_out, and_9_out,
       and_10_out, and_11_out, and_12_out, and_13_out, and_14_out, and_15_out, and_16_out, and_17_out,
       and_18_out, and_19_out, and_20_out, and_21_out, and_22_out, and_23_out, and_24_out, and_25_out,
       and_26_out, and_27_out, and_28_out, and_29_out, and_30_out, and_31_out, and_32_out, and_33_out,
       and_34_out, and_35_out, clock_1_out, d_ff_4_qn, d_ff_7_qn, d_ff_11_qn, d_ff_14_qn, d_ff_19_qn,
       multiplexer_1_out, multiplexer_2_out, multiplexer_3_out, multiplexer_4_out, multiplexer_5_out,
       multiplexer_6_out, multiplexer_7_out, multiplexer_8_out, multiplexer_9_out, multiplexer_10_out,
       multiplexer_11_out, multiplexer_12_out, multiplexer_13_out, multiplexer_14_out, multiplexer_15_out,
       multiplexer_16_out, multiplexer_17_out, multiplexer_18_out, multiplexer_19_out, not_1_out, not_2_out,
       not_3_out, not_4_out, not_5_out, not_6_out, not_7_out, not_8_out, not_9_out, not_10_out, not_11_out,
       xor_1_out, xor_2_out, xor_3_out, xor_4_out, xor_5_out, xor_6_out, xor_7_out, xor_8_out, xor_9_out,
       xor_10_out, xor_11_out, xor_12_out, xor_13_out, xor_14_out;
  wire [2:0] d_ff_7_q, d_ff_14_q;
  wire [3:0] bit_extender_1_out, bit_extender_2_out, d_ff_4_q, d_ff_11_q;
  wire [4:0] d_ff_19_q, divider_1_out, divider_1_rem;

  Clock clock_1 (.out(clock_1_out));
  and and_1 (and_1_out, d_ff_4_qn, not_5_out);
  and and_2 (and_2_out, d_ff_7_qn, not_4_out);
  Multiplexer multiplexer_1 (.in0(d_ff_4_q[3]), .in1(and_10_out), .out(multiplexer_1_out), .sel(1'b1), .en(1'b1));
  Multiplexer multiplexer_2 (.in0(d_ff_4_q[2]), .in1(and_11_out), .out(multiplexer_2_out), .sel(1'b1), .en(1'b1));
  Multiplexer multiplexer_3 (.in0(d_ff_4_q[1]), .in1(and_7_out), .out(multiplexer_3_out), .sel(1'b1), .en(1'b1));
  Multiplexer multiplexer_4 (.in0(d_ff_4_q[0]), .in1(and_1_out), .out(multiplexer_4_out), .sel(1'b1), .en(1'b1));
  Multiplexer multiplexer_5 (.in0(d_ff_7_q[2]), .in1(and_12_out), .out(multiplexer_5_out), .sel(and_8_out), .en(1'b1));
  Multiplexer multiplexer_6 (.in0(d_ff_7_q[1]), .in1(and_9_out), .out(multiplexer_6_out), .sel(and_8_out), .en(1'b1));
  Multiplexer multiplexer_7 (.in0(d_ff_7_q[0]), .in1(and_2_out), .out(multiplexer_7_out), .sel(and_8_out), .en(1'b1));
  D_Flip_Flop d_ff_1 (.clk(clock_1_out), .D(multiplexer_1_out), .Q(d_ff_4_q[3]));  // open: Qn, preset, en, reset
  D_Flip_Flop d_ff_2 (.clk(clock_1_out), .D(multiplexer_2_out), .Q(d_ff_4_q[2]));  // open: Qn, preset, en, reset
  D_Flip_Flop d_ff_3 (.clk(clock_1_out), .D(multiplexer_3_out), .Q(d_ff_4_q[1]));  // open: Qn, preset, en, reset
  D_Flip_Flop d_ff_4 (
    .clk(clock_1_out), .D(multiplexer_4_out), .Q(d_ff_4_q[0]), .Qn(d_ff_4_qn));  // open: preset, en, reset
  D_Flip_Flop d_ff_5 (.clk(clock_1_out), .D(multiplexer_5_out), .Q(d_ff_7_q[2]));  // open: Qn, preset, en, reset
  D_Flip_Flop d_ff_6 (.clk(clock_1_out), .D(multiplexer_6_out), .Q(d_ff_7_q[1]));  // open: Qn, preset, en, reset
  D_Flip_Flop d_ff_7 (
    .clk(clock_1_out), .D(multiplexer_7_out), .Q(d_ff_7_q[0]), .Qn(d_ff_7_qn));  // open: preset, en, reset
  not not_1 (not_1_out, d_ff_4_q[2]);
  not not_2 (not_2_out, d_ff_4_q[1]);
  and and_3 (and_3_out, d_ff_7_q[1], d_ff_7_q[0]);
  not not_3 (not_3_out, d_ff_7_q[1]);
  and and_4 (and_4_out, d_ff_4_q[2], d_ff_4_q[1], d_ff_4_q[0]);
  and and_5 (and_5_out, d_ff_4_q[1], d_ff_4_q[0]);
  xor xor_1 (xor_1_out, d_ff_4_q[1], d_ff_4_q[0]);
  and and_6 (and_6_out, d_ff_7_q[2], not_3_out, d_ff_7_q[0]);
  xor xor_2 (xor_2_out, d_ff_4_q[3], and_4_out);
  xor xor_3 (xor_3_out, d_ff_4_q[2], and_5_out);
  and and_7 (and_7_out, xor_1_out, not_5_out);
  and and_8 (and_8_out, d_ff_4_q[3], not_1_out, not_2_out, d_ff_4_q[0]);
  xor xor_4 (xor_4_out, d_ff_7_q[2], and_3_out);
  not not_4 (not_4_out, and_6_out);
  and and_9 (and_9_out, not_4_out, xor_5_out);
  xor xor_5 (xor_5_out, d_ff_7_q[1], d_ff_7_q[0]);
  and and_10 (and_10_out, xor_2_out, not_5_out);
  and and_11 (and_11_out, xor_3_out, not_5_out);
  not not_5 (not_5_out, and_8_out);
  and and_12 (and_12_out, xor_4_out, not_4_out);
  Hex_Digit_Display hex_digit_display_1 (.value(d_ff_4_q));  // open: dp
  Hex_Digit_Display hex_digit_display_2 (.value({1'b0, d_ff_7_q}));  // open: dp
  and and_13 (and_13_out, and_8_out, and_6_out);
  and and_14 (and_14_out, d_ff_11_qn, not_10_out);
  and and_15 (and_15_out, d_ff_14_qn, not_9_out);
  Multiplexer multiplexer_8 (
    .in0(d_ff_11_q[3]), .in1(and_25_out), .out(multiplexer_8_out), .sel(and_13_out), .en(1'b1));
  Multiplexer multiplexer_9 (
    .in0(d_ff_11_q[2]), .in1(and_21_out), .out(multiplexer_9_out), .sel(and_13_out), .en(1'b1));
  Multiplexer multiplexer_10 (
    .in0(d_ff_11_q[1]), .in1(and_19_out), .out(multiplexer_10_out), .sel(and_13_out), .en(1'b1));
  Multiplexer multiplexer_11 (
    .in0(d_ff_11_q[0]), .in1(and_14_out), .out(multiplexer_11_out), .sel(and_13_out), .en(1'b1));
  Multiplexer multiplexer_12 (
    .in0(d_ff_14_q[2]), .in1(and_23_out), .out(multiplexer_12_out), .sel(and_22_out), .en(1'b1));
  Multiplexer multiplexer_13 (
    .in0(d_ff_14_q[1]), .in1(and_24_out), .out(multiplexer_13_out), .sel(and_22_out), .en(1'b1));
  Multiplexer multiplexer_14 (
    .in0(d_ff_14_q[0]), .in1(and_15_out), .out(multiplexer_14_out), .sel(and_22_out), .en(1'b1));
  D_Flip_Flop d_ff_8 (.clk(clock_1_out), .D(multiplexer_8_out), .Q(d_ff_11_q[3]));  // open: Qn, preset, en, reset
  D_Flip_Flop d_ff_9 (.clk(clock_1_out), .D(multiplexer_9_out), .Q(d_ff_11_q[2]));  // open: Qn, preset, en, reset
  D_Flip_Flop d_ff_10 (.clk(clock_1_out), .D(multiplexer_10_out), .Q(d_ff_11_q[1]));  // open: Qn, preset, en, reset
  D_Flip_Flop d_ff_11 (
    .clk(clock_1_out), .D(multiplexer_11_out), .Q(d_ff_11_q[0]), .Qn(d_ff_11_qn));  // open: preset, en, reset
  D_Flip_Flop d_ff_12 (.clk(clock_1_out), .D(multiplexer_12_out), .Q(d_ff_14_q[2]));  // open: Qn, preset, en, reset
  D_Flip_Flop d_ff_13 (.clk(clock_1_out), .D(multiplexer_13_out), .Q(d_ff_14_q[1]));  // open: Qn, preset, en, reset
  D_Flip_Flop d_ff_14 (
    .clk(clock_1_out), .D(multiplexer_14_out), .Q(d_ff_14_q[0]), .Qn(d_ff_14_qn));  // open: preset, en, reset
  and and_16 (and_16_out, d_ff_11_q[1], d_ff_11_q[0]);
  xor xor_6 (xor_6_out, d_ff_11_q[1], d_ff_11_q[0]);
  not not_6 (not_6_out, d_ff_11_q[2]);
  not not_7 (not_7_out, d_ff_11_q[1]);
  and and_17 (and_17_out, d_ff_14_q[1], d_ff_14_q[0]);
  not not_8 (not_8_out, d_ff_14_q[1]);
  and and_18 (and_18_out, d_ff_11_q[2], d_ff_11_q[1], d_ff_11_q[0]);
  xor xor_7 (xor_7_out, d_ff_11_q[2], and_16_out);
  and and_19 (and_19_out, xor_6_out, not_10_out);
  xor xor_8 (xor_8_out, d_ff_14_q[2], and_17_out);
  and and_20 (and_20_out, d_ff_14_q[2], not_8_out, d_ff_14_q[0]);
  xor xor_9 (xor_9_out, d_ff_11_q[3], and_18_out);
  and and_21 (and_21_out, xor_7_out, not_10_out);
  and and_22 (and_22_out, d_ff_11_q[3], not_6_out, not_7_out, d_ff_11_q[0]);
  and and_23 (and_23_out, xor_8_out, not_9_out);
  xor xor_10 (xor_10_out, d_ff_14_q[1], d_ff_14_q[0]);
  and and_24 (and_24_out, xor_10_out, not_9_out);
  not not_9 (not_9_out, and_20_out);
  and and_25 (and_25_out, xor_9_out, not_10_out);
  not not_10 (not_10_out, and_22_out);
  Hex_Digit_Display hex_digit_display_3 (.value(d_ff_11_q));  // open: dp
  Hex_Digit_Display hex_digit_display_4 (.value({1'b0, d_ff_14_q}));  // open: dp
  and and_26 (and_26_out, and_13_out, and_20_out);
  Multiplexer multiplexer_15 (
    .in0(d_ff_19_q[4]), .in1(and_35_out), .out(multiplexer_15_out), .sel(and_26_out), .en(1'b1));
  Multiplexer multiplexer_16 (
    .in0(d_ff_19_q[3]), .in1(and_33_out), .out(multiplexer_16_out), .sel(and_26_out), .en(1'b1));
  Multiplexer multiplexer_17 (
    .in0(d_ff_19_q[2]), .in1(and_34_out), .out(multiplexer_17_out), .sel(and_26_out), .en(1'b1));
  Multiplexer multiplexer_18 (
    .in0(d_ff_19_q[1]), .in1(and_30_out), .out(multiplexer_18_out), .sel(and_26_out), .en(1'b1));
  Multiplexer multiplexer_19 (
    .in0(d_ff_19_q[0]), .in1(and_31_out), .out(multiplexer_19_out), .sel(and_26_out), .en(1'b1));
  D_Flip_Flop d_ff_15 (.clk(clock_1_out), .D(multiplexer_15_out), .Q(d_ff_19_q[4]));  // open: Qn, preset, en, reset
  D_Flip_Flop d_ff_16 (.clk(clock_1_out), .D(multiplexer_16_out), .Q(d_ff_19_q[3]));  // open: Qn, preset, en, reset
  D_Flip_Flop d_ff_17 (.clk(clock_1_out), .D(multiplexer_17_out), .Q(d_ff_19_q[2]));  // open: Qn, preset, en, reset
  D_Flip_Flop d_ff_18 (.clk(clock_1_out), .D(multiplexer_18_out), .Q(d_ff_19_q[1]));  // open: Qn, preset, en, reset
  D_Flip_Flop d_ff_19 (
    .clk(clock_1_out), .D(multiplexer_19_out), .Q(d_ff_19_q[0]), .Qn(d_ff_19_qn));  // open: preset, en, reset
  and and_27 (and_27_out, d_ff_19_q[2], d_ff_19_q[1], d_ff_19_q[0]);
  and and_28 (and_28_out, d_ff_19_q[1], d_ff_19_q[0]);
  xor xor_11 (xor_11_out, d_ff_19_q[1], d_ff_19_q[0]);
  and and_29 (and_29_out, d_ff_19_q[3], d_ff_19_q[2], d_ff_19_q[1], d_ff_19_q[0]);
  xor xor_12 (xor_12_out, d_ff_19_q[3], and_27_out);
  xor xor_13 (xor_13_out, d_ff_19_q[2], and_28_out);
  and and_30 (and_30_out, xor_11_out, not_11_out);
  and and_31 (and_31_out, d_ff_19_qn, not_11_out);
  and and_32 (and_32_out, d_ff_19_q[4], d_ff_19_q[2], d_ff_19_q[1], d_ff_19_q[0]);
  xor xor_14 (xor_14_out, d_ff_19_q[4], and_29_out);
  and and_33 (and_33_out, xor_12_out, not_11_out);
  and and_34 (and_34_out, xor_13_out, not_11_out);
  not not_11 (not_11_out, and_32_out);
  and and_35 (and_35_out, xor_14_out, not_11_out);
  Divider #(.width(5)) divider_1 (
    .a(d_ff_19_q), .b(5'b01010), .out(divider_1_out), .rem(divider_1_rem));  // open: upper
  Hex_Digit_Display hex_digit_display_5 (.value(bit_extender_1_out));  // open: dp
  Hex_Digit_Display hex_digit_display_6 (.value(bit_extender_2_out));  // open: dp
  Bit_Extender #(.in_width(5), .out_width(4)) bit_extender_1 (.in(divider_1_out), .out(bit_extender_1_out));
  Bit_Extender #(.in_width(5), .out_width(4)) bit_extender_2 (.in(divider_1_rem), .out(bit_extender_2_out));

  // Notes on the sheet:
  //   Q3
  //   Q2
  //   Q1
  //   Q0
  //   T2
  //   T1
  //   T0
  //   MU3
  //   MU2
  //   MU1
  //   MU0
  //   MT2
  //   MT1
  //   MT0
  //   H4
  //   H3
  //   H2
  //   H1
  //   H0
endmodule
