// Logisim project de pro c6.circ as structural Verilog: 1 circuit, main circuit main
module main (
);

  wire and_1_out, and_2_out, and_3_out, and_4_out, and_5_out, and_6_out, and_7_out, and_8_out, and_9_out,
       and_10_out, and_11_out, clock_1_out, d_ff_1_q, d_ff_2_q, d_ff_3_q, d_ff_4_q, d_ff_4_qn, d_ff_5_q,
       d_ff_5_qn, d_ff_6_q, d_ff_6_qn, not_1_out, xor_1_out, xor_2_out, xor_3_out, xor_4_out, xor_5_out;

  Clock clock_1 (.out(clock_1_out));
  xor xor_1 (xor_1_out, d_ff_1_q, and_11_out);
  and and_1 (and_1_out, xor_1_out, not_1_out);
  and and_2 (and_2_out, d_ff_4_q, d_ff_5_q, d_ff_6_q);
  and and_3 (and_3_out, d_ff_5_q, d_ff_6_q);
  xor xor_2 (xor_2_out, d_ff_5_q, d_ff_6_q);
  and and_4 (and_4_out, d_ff_6_qn, not_1_out);
  D_Flip_Flop d_ff_1 (.clk(clock_1_out), .D(and_1_out), .Q(d_ff_1_q));  // open: Qn, preset, en, reset
  D_Flip_Flop d_ff_2 (.clk(clock_1_out), .D(and_7_out), .Q(d_ff_2_q));  // open: Qn, preset, en, reset
  D_Flip_Flop d_ff_3 (.clk(clock_1_out), .D(and_8_out), .Q(d_ff_3_q));  // open: Qn, preset, en, reset
  xor xor_3 (xor_3_out, d_ff_4_q, and_3_out);
  D_Flip_Flop d_ff_4 (.clk(clock_1_out), .D(and_6_out), .Q(d_ff_4_q), .Qn(d_ff_4_qn));  // open: preset, en, reset
  and and_5 (and_5_out, xor_2_out, d_ff_5_qn);
  D_Flip_Flop d_ff_5 (.clk(clock_1_out), .D(and_5_out), .Q(d_ff_5_q), .Qn(d_ff_5_qn));  // open: preset, en, reset
  D_Flip_Flop d_ff_6 (.clk(clock_1_out), .D(and_4_out), .Q(d_ff_6_q), .Qn(d_ff_6_qn));  // open: preset, en, reset
  xor xor_4 (xor_4_out, d_ff_2_q, and_10_out);
  xor xor_5 (xor_5_out, d_ff_3_q, and_2_out);
  and and_6 (and_6_out, xor_3_out, not_1_out);
  and and_7 (and_7_out, xor_4_out, not_1_out);
  and and_8 (and_8_out, xor_5_out, not_1_out);
  and and_9 (and_9_out, d_ff_1_q, d_ff_2_q, d_ff_3_q, d_ff_4_qn, d_ff_5_q, d_ff_6_q);
  not not_1 (not_1_out, and_9_out);
  and and_10 (and_10_out, d_ff_3_q, d_ff_4_q, d_ff_5_q, d_ff_6_q);
  and and_11 (and_11_out, d_ff_2_q, d_ff_3_q, d_ff_4_q, d_ff_5_q, d_ff_6_q);
  LED led_1 (.in(d_ff_1_q));
  LED led_2 (.in(d_ff_2_q));
  LED led_3 (.in(d_ff_3_q));
  LED led_4 (.in(d_ff_4_q));
  LED led_5 (.in(d_ff_5_q));
  LED led_6 (.in(d_ff_6_q));

  // Notes on the sheet:
  //   Q5
  //   Q4
  //   Q3
  //   Q2
  //   Q1
  //   Q0
endmodule
