// Logisim project de pro c7.circ as structural Verilog: 1 circuit, main circuit main
module main (
  input  V,
  input  F,
  input  P
);

  wire and_1_out, and_2_out, clock_1_out, d_ff_1_q, d_ff_1_qn, not_1_out, not_2_out, or_1_out;

  Clock clock_1 (.out(clock_1_out));
  not not_1 (not_1_out, F);
  not not_2 (not_2_out, P);
  D_Flip_Flop d_ff_1 (.clk(clock_1_out), .D(or_1_out), .Q(d_ff_1_q), .Qn(d_ff_1_qn));  // open: preset, en, reset
  and and_1 (and_1_out, d_ff_1_qn, V, not_1_out);
  and and_2 (and_2_out, d_ff_1_q, not_2_out);
  or or_1 (or_1_out, and_1_out, and_2_out);
  LED led_1 (.in(d_ff_1_q));
  LED led_2 (.in(d_ff_1_q));

  // Notes on the sheet:
  //   B
  //   G
endmodule
