// Logisim project de pro c8.circ as structural Verilog: 1 circuit, main circuit main
module main (
  input  in_1,
  input  in_2,
  input  in_3,
  input  in_4,
  input  in_5,
  input  in_6,
  input  in_7,
  input  in_8,
  input  in_9,
  input  in_10,
  input  in_11,
  output out_12,
  output out_13,
  output out_14,
  output out_15,
  output out_16
);

  wire adder_1_cout, adder_2_cout, adder_3_cout, clock_1_out, xor_1_out, xor_2_out, xor_3_out, xor_4_out;
  wire [3:0] counter_1_q;

  xor xor_1 (xor_1_out, in_6, in_11);
  Adder #(.width(1)) adder_1 (.a(in_1), .b(xor_1_out), .out(out_13), .cin(in_11), .cout(adder_1_cout));
  Adder #(.width(1)) adder_2 (.a(in_2), .b(xor_2_out), .out(out_14), .cin(adder_1_cout), .cout(adder_2_cout));
  xor xor_2 (xor_2_out, in_7, in_11);
  xor xor_3 (xor_3_out, in_8, in_11);
  Adder #(.width(1)) adder_3 (.a(in_3), .b(xor_3_out), .out(out_15), .cin(adder_2_cout), .cout(adder_3_cout));
  xor xor_4 (xor_4_out, in_9, in_11);
  Adder #(.width(1)) adder_4 (.a(in_4), .b(xor_4_out), .out(out_16), .cin(adder_3_cout), .cout(out_12));
  Clock clock_1 (.out(clock_1_out));
  Counter #(.width(4), .max('hf)) counter_1 (
    .count(in_5), .Q(counter_1_q), .clk(clock_1_out), .clr(in_10));  // open: load, D, carry
  Hex_Digit_Display hex_digit_display_1 (.value(counter_1_q));  // open: dp

  // Notes on the sheet:
  //   4-bit ALU
  //   A 4-bit COUNTER
endmodule
