// Logisim project de pro c9.circ as structural Verilog: 1 circuit, main circuit main
module main (
  input  in_1,
  input  in_2,
  output out_3
);

  wire comparator_1_gt;

  Comparator #(.width(1)) comparator_1 (.a(in_1), .b(in_2), .gt(comparator_1_gt));  // open: eq, lt
  Multiplexer multiplexer_1 (.in0(in_1), .in1(in_2), .out(out_3), .sel(comparator_1_gt));  // open: en
endmodule
